// Logisim project RISC-V Single Cycle Datapath.circ as structural Verilog
module main (
  input  in_1,
  input  in_2,
  input  in_3,
  output [31:0] out_4,
  output [23:0] out_5,
  output [3:0] out_6
);

  wire and_1_out, CLK, control_unit_1_branch, control_unit_1_jump, control_unit_1_jumpreg,
       control_unit_1_memtoreg, control_unit_1_memwrite, control_unit_1_regwrite, control_unit_1_retaddr,
       control_unit_1_rs1, control_unit_1_rs2, control_unit_1_upperimm, or_1_out;
  wire [2:0] control_unit_1_a0;
  wire [6:0] ram_1_data;
  wire [31:0] adder_1_out, ImmediateGen_immediateout, multiplexer_1_out, multiplexer_2_out,
       multiplexer_3_out, multiplexer_4_out, multiplexer_5_out, multiplexer_6_out, multiplexer_7_out, PC_q,
       ram_2_data, Register_File_readdata1, Register_File_readdata2;
  wire [31:7] ram_1_data_2;

  Control_Unit control_unit_1 (
    .OpcodeInput(ram_1_data), .RS1(control_unit_1_rs1), .Branch(control_unit_1_branch),
    .RetAddr(control_unit_1_retaddr), .MemToReg(control_unit_1_memtoreg), .UpperImm(control_unit_1_upperimm),
    .JumpReg(control_unit_1_jumpreg), .MemWrite(control_unit_1_memwrite), .RS2(control_unit_1_rs2),
    .RegWrite(control_unit_1_regwrite), .A2(control_unit_1_a0[2]), .A1(control_unit_1_a0[1]),
    .A0(control_unit_1_a0[0]), .Jump(control_unit_1_jump));
  and and_1 (and_1_out, out_4[0], control_unit_1_branch);
  Multiplexer #(.width(32), .enable("false")) multiplexer_1 (
    .in0(PC_q), .in1(Register_File_readdata1), .out(multiplexer_1_out), .sel(control_unit_1_jumpreg));
  or or_1 (or_1_out, and_1_out, control_unit_1_jump);
  Multiplexer #(.width(32), .enable("false")) multiplexer_2 (
    .in0(32'h4), .in1(ImmediateGen_immediateout), .out(multiplexer_2_out), .sel(or_1_out));
  Register #(.width(32)) PC (.D(adder_1_out), .Q(PC_q), .clk(CLK), .clr(in_3));  // open: en
  Adder #(.width(32)) adder_1 (.a(multiplexer_1_out), .b(multiplexer_2_out), .out(adder_1_out));  // open: cin, cout
  RAM #(.addrWidth(24), .dataWidth(32)) ram_1 (
    .addr(PC_q[25:2]), .data({ram_1_data_2, ram_1_data}), .clk(CLK), .clr(in_2));  // open: sel, ld
  Multiplexer #(.width(32), .enable("false")) multiplexer_3 (
    .in0(out_4), .in1(ram_2_data), .out(multiplexer_3_out), .sel(control_unit_1_memtoreg));
  Immediate_Generator ImmediateGen (.Instruction({ram_1_data_2, ram_1_data}), .ImmediateOut(ImmediateGen_immediateout));
  ALU_Control ALU_Control (
    .ALUOp(control_unit_1_a0), .Function3(ram_1_data_2[14:12]), .Function7(ram_1_data_2[31:25]),
    .ALUOperation(out_6));
  Register_File Register_File (
    .WriteReg_CU(control_unit_1_regwrite), .WriteAddress(ram_1_data_2[11:7]), .WriteData(multiplexer_3_out),
    .CLK(CLK), .ReadReg1(ram_1_data_2[19:15]), .Reset(in_3), .ReadReg2(ram_1_data_2[24:20]),
    .ReadData1(Register_File_readdata1), .ReadData2(Register_File_readdata2));  // open: out_10
  Multiplexer #(.width(32), .enable("false")) multiplexer_4 (
    .in0(PC_q), .in1(Register_File_readdata1), .out(multiplexer_4_out), .sel(control_unit_1_rs1));
  Multiplexer #(.width(32), .enable("false")) multiplexer_5 (
    .in0(ImmediateGen_immediateout), .in1(Register_File_readdata2), .out(multiplexer_5_out),
    .sel(control_unit_1_rs2));
  Multiplexer #(.width(32), .enable("false")) multiplexer_6 (
    .in0(multiplexer_4_out), .in1({32{1'b0}}), .out(multiplexer_6_out), .sel(control_unit_1_upperimm));
  Multiplexer #(.width(32), .enable("false")) multiplexer_7 (
    .in0(multiplexer_5_out), .in1(32'h4), .out(multiplexer_7_out), .sel(control_unit_1_retaddr));
  ALU ALU (.dataA(multiplexer_6_out), .DataB(multiplexer_7_out), .ALUOperation(out_6), .ALUOutput(out_4));
  RAM #(.addrWidth(24), .dataWidth(32), .bus("separate")) ram_2 (
    .addr(out_4[23:0]), .din(Register_File_readdata2), .data(ram_2_data), .str(control_unit_1_memwrite),
    .clk(CLK), .ld(control_unit_1_memtoreg), .clr(in_1));  // open: sel
  Clock clock_1 (.out(CLK));

  assign out_5 = out_4[23:0];

  // Other names for the same wires on the sheet: Reset = in_3
endmodule

module Full_Adder (
  input  in_1,
  input  in_2,
  input  in_3,
  output out_4,
  output out_5
);

  wire and_1_out, and_2_out, xor_1_out;

  xor xor_1 (xor_1_out, in_3, in_2);
  xor xor_2 (out_4, xor_1_out, in_1);
  and and_1 (and_1_out, xor_1_out, in_1);
  and and_2 (and_2_out, in_3, in_2);
  or or_1 (out_5, and_1_out, and_2_out);
endmodule

module _4_Bit_Parallel_Adder (
  input  [3:0] in_1,
  input  in_2,
  input  [3:0] in_3,
  output out_4,
  output [3:0] out_5
);

  wire full_adder_2_out_5, full_adder_3_out_5, full_adder_4_out_5;

  Full_Adder full_adder_1 (.in_1(full_adder_2_out_5), .in_2(in_3[3]), .in_3(in_1[3]), .out_4(out_5[3]), .out_5(out_4));
  Full_Adder full_adder_2 (
    .in_1(full_adder_3_out_5), .in_2(in_3[2]), .in_3(in_1[2]), .out_4(out_5[2]), .out_5(full_adder_2_out_5));
  Full_Adder full_adder_3 (
    .in_1(full_adder_4_out_5), .in_2(in_3[1]), .in_3(in_1[1]), .out_4(out_5[1]), .out_5(full_adder_3_out_5));
  Full_Adder full_adder_4 (.in_1(in_2), .in_2(in_3[0]), .in_3(in_1[0]), .out_4(out_5[0]), .out_5(full_adder_4_out_5));

  // Notes on the sheet:
  //   in_1: pull=up
endmodule

module _32_Bit_Adder (
  input  [31:0] in_1,
  input  [31:0] in_2,
  output [31:0] out_3
);

  wire n4_bit_parallel_adder_2_out_4, n4_bit_parallel_adder_3_out_4, n4_bit_parallel_adder_4_out_4,
       n4_bit_parallel_adder_5_out_4, n4_bit_parallel_adder_6_out_4, n4_bit_parallel_adder_7_out_4,
       n4_bit_parallel_adder_8_out_4;

  _4_Bit_Parallel_Adder u_4_bit_parallel_adder_1 (
    .in_1(in_1[31:28]), .in_2(n4_bit_parallel_adder_2_out_4), .in_3(in_2[31:28]), .out_5(out_3[31:28]));  // open: out_4
  _4_Bit_Parallel_Adder u_4_bit_parallel_adder_2 (
    .in_1(in_1[27:24]), .in_2(n4_bit_parallel_adder_3_out_4), .in_3(in_2[27:24]),
    .out_4(n4_bit_parallel_adder_2_out_4), .out_5(out_3[27:24]));
  _4_Bit_Parallel_Adder u_4_bit_parallel_adder_3 (
    .in_1(in_1[23:20]), .in_2(n4_bit_parallel_adder_4_out_4), .in_3(in_2[23:20]),
    .out_4(n4_bit_parallel_adder_3_out_4), .out_5(out_3[23:20]));
  _4_Bit_Parallel_Adder u_4_bit_parallel_adder_4 (
    .in_1(in_1[19:16]), .in_2(n4_bit_parallel_adder_5_out_4), .in_3(in_2[19:16]),
    .out_4(n4_bit_parallel_adder_4_out_4), .out_5(out_3[19:16]));
  _4_Bit_Parallel_Adder u_4_bit_parallel_adder_5 (
    .in_1(in_1[15:12]), .in_2(n4_bit_parallel_adder_6_out_4), .in_3(in_2[15:12]),
    .out_4(n4_bit_parallel_adder_5_out_4), .out_5(out_3[15:12]));
  _4_Bit_Parallel_Adder u_4_bit_parallel_adder_6 (
    .in_1(in_1[11:8]), .in_2(n4_bit_parallel_adder_7_out_4), .in_3(in_2[11:8]),
    .out_4(n4_bit_parallel_adder_6_out_4), .out_5(out_3[11:8]));
  _4_Bit_Parallel_Adder u_4_bit_parallel_adder_7 (
    .in_1(in_1[7:4]), .in_2(n4_bit_parallel_adder_8_out_4), .in_3(in_2[7:4]),
    .out_4(n4_bit_parallel_adder_7_out_4), .out_5(out_3[7:4]));
  _4_Bit_Parallel_Adder u_4_bit_parallel_adder_8 (
    .in_1(in_1[3:0]), .in_2(1'b0), .in_3(in_2[3:0]), .out_4(n4_bit_parallel_adder_8_out_4), .out_5(out_3[3:0]));
endmodule

module Full_Subtractor (
  input  in_1,
  input  in_2,
  input  in_3,
  output out_4,
  output out_5
);

  wire and_1_out, and_2_out, not_1_out, not_2_out, xor_1_out;

  xor xor_1 (xor_1_out, in_3, in_2);
  not not_1 (not_1_out, xor_1_out);
  not not_2 (not_2_out, in_3);
  xor xor_2 (out_4, xor_1_out, in_1);
  and and_1 (and_1_out, not_1_out, in_1);
  and and_2 (and_2_out, not_2_out, in_2);
  or or_1 (out_5, and_1_out, and_2_out);
endmodule

module _4_Bit_Parallel_Subtractor (
  input  [3:0] in_1,
  input  in_2,
  input  [3:0] in_3,
  output out_4,
  output [3:0] out_5
);

  wire full_subtractor_2_out_5, full_subtractor_3_out_5, full_subtractor_4_out_5;

  Full_Subtractor full_subtractor_1 (
    .in_1(full_subtractor_2_out_5), .in_2(in_3[3]), .in_3(in_1[3]), .out_4(out_5[3]), .out_5(out_4));
  Full_Subtractor full_subtractor_2 (
    .in_1(full_subtractor_3_out_5), .in_2(in_3[2]), .in_3(in_1[2]), .out_4(out_5[2]),
    .out_5(full_subtractor_2_out_5));
  Full_Subtractor full_subtractor_3 (
    .in_1(full_subtractor_4_out_5), .in_2(in_3[1]), .in_3(in_1[1]), .out_4(out_5[1]),
    .out_5(full_subtractor_3_out_5));
  Full_Subtractor full_subtractor_4 (
    .in_1(in_2), .in_2(in_3[0]), .in_3(in_1[0]), .out_4(out_5[0]), .out_5(full_subtractor_4_out_5));
endmodule

module _32_Bit_Subtractor (
  input  [31:0] in_1,
  input  [31:0] in_2,
  output [31:0] out_3
);

  wire n4_bit_parallel_subtractor_2_out_4, n4_bit_parallel_subtractor_3_out_4,
       n4_bit_parallel_subtractor_4_out_4, n4_bit_parallel_subtractor_5_out_4,
       n4_bit_parallel_subtractor_6_out_4, n4_bit_parallel_subtractor_7_out_4,
       n4_bit_parallel_subtractor_8_out_4;

  _4_Bit_Parallel_Subtractor u_4_bit_parallel_subtractor_1 (
    .in_1(in_1[31:28]), .in_2(n4_bit_parallel_subtractor_2_out_4), .in_3(in_2[31:28]), .out_5(out_3[31:28]));  // open: out_4
  _4_Bit_Parallel_Subtractor u_4_bit_parallel_subtractor_2 (
    .in_1(in_1[27:24]), .in_2(n4_bit_parallel_subtractor_3_out_4), .in_3(in_2[27:24]),
    .out_4(n4_bit_parallel_subtractor_2_out_4), .out_5(out_3[27:24]));
  _4_Bit_Parallel_Subtractor u_4_bit_parallel_subtractor_3 (
    .in_1(in_1[23:20]), .in_2(n4_bit_parallel_subtractor_4_out_4), .in_3(in_2[23:20]),
    .out_4(n4_bit_parallel_subtractor_3_out_4), .out_5(out_3[23:20]));
  _4_Bit_Parallel_Subtractor u_4_bit_parallel_subtractor_4 (
    .in_1(in_1[19:16]), .in_2(n4_bit_parallel_subtractor_5_out_4), .in_3(in_2[19:16]),
    .out_4(n4_bit_parallel_subtractor_4_out_4), .out_5(out_3[19:16]));
  _4_Bit_Parallel_Subtractor u_4_bit_parallel_subtractor_5 (
    .in_1(in_1[15:12]), .in_2(n4_bit_parallel_subtractor_6_out_4), .in_3(in_2[15:12]),
    .out_4(n4_bit_parallel_subtractor_5_out_4), .out_5(out_3[15:12]));
  _4_Bit_Parallel_Subtractor u_4_bit_parallel_subtractor_6 (
    .in_1(in_1[11:8]), .in_2(n4_bit_parallel_subtractor_7_out_4), .in_3(in_2[11:8]),
    .out_4(n4_bit_parallel_subtractor_6_out_4), .out_5(out_3[11:8]));
  _4_Bit_Parallel_Subtractor u_4_bit_parallel_subtractor_7 (
    .in_1(in_1[7:4]), .in_2(n4_bit_parallel_subtractor_8_out_4), .in_3(in_2[7:4]),
    .out_4(n4_bit_parallel_subtractor_7_out_4), .out_5(out_3[7:4]));
  _4_Bit_Parallel_Subtractor u_4_bit_parallel_subtractor_8 (
    .in_1(in_1[3:0]), .in_2(1'b0), .in_3(in_2[3:0]), .out_4(n4_bit_parallel_subtractor_8_out_4),
    .out_5(out_3[3:0]));
endmodule

module ALU (
  input  [31:0] dataA,
  input  [31:0] DataB,
  input  [3:0] ALUOperation,
  output [31:0] ALUOutput
);

  wire comparator_1_eq, comparator_1_lt, comparator_2_lt, not_1_out, not_2_out, not_3_out;
  wire [31:0] and_1_out, bit_extender_1_out, bit_extender_2_out, bit_extender_3_out, bit_extender_4_out,
       bit_extender_5_out, bit_extender_6_out, n32_bit_adder_1_out_3, n32_bit_subtractor_1_out_3, or_1_out,
       shifter_1_out, shifter_2_out, shifter_3_out, xor_1_out;

  assign or_1_out = dataA | DataB;  // OR_Gate or_1, 32 bits wide
  _32_Bit_Adder u_32_bit_adder_1 (.in_1(dataA), .in_2(DataB), .out_3(n32_bit_adder_1_out_3));
  _32_Bit_Subtractor u_32_bit_subtractor_1 (.in_1(dataA), .in_2(DataB), .out_3(n32_bit_subtractor_1_out_3));
  Comparator #(.width(32)) comparator_1 (.a(dataA), .b(DataB), .eq(comparator_1_eq), .lt(comparator_1_lt));  // open: gt
  Shifter #(.width(32)) shifter_1 (.in(dataA), .\dist (DataB[4:0]), .out(shifter_1_out));
  assign xor_1_out = dataA ^ DataB;  // XOR_Gate xor_1, 32 bits wide
  Shifter #(.width(32), .shift("lr")) shifter_2 (.in(dataA), .\dist (DataB[4:0]), .out(shifter_2_out));
  Shifter #(.width(32), .shift("ar")) shifter_3 (.in(dataA), .\dist (DataB[4:0]), .out(shifter_3_out));
  Comparator #(.width(32), .mode("unsigned")) comparator_2 (
    .a(dataA), .b(DataB), .lt(comparator_2_lt));  // open: gt, eq
  assign and_1_out = dataA & DataB;  // AND_Gate and_1, 32 bits wide
  not not_1 (not_1_out, comparator_1_lt);
  not not_2 (not_2_out, comparator_1_eq);
  not not_3 (not_3_out, comparator_2_lt);
  assign bit_extender_1_out = {{31{1'b0}}, not_1_out};  // Bit_Extender bit_extender_1
  assign bit_extender_2_out = {{31{1'b0}}, comparator_1_lt};  // Bit_Extender bit_extender_2
  assign bit_extender_3_out = {{31{1'b0}}, comparator_1_eq};  // Bit_Extender bit_extender_3
  assign bit_extender_4_out = {{31{1'b0}}, not_2_out};  // Bit_Extender bit_extender_4
  assign bit_extender_5_out = {{31{1'b0}}, not_3_out};  // Bit_Extender bit_extender_5
  assign bit_extender_6_out = {{31{1'b0}}, comparator_2_lt};  // Bit_Extender bit_extender_6
  Multiplexer #(.select(4), .width(32), .enable("false")) multiplexer_1 (
    .in0(or_1_out), .in1(and_1_out), .in2(n32_bit_adder_1_out_3), .in3(n32_bit_subtractor_1_out_3),
    .in4(bit_extender_1_out), .in5(bit_extender_2_out), .in6(bit_extender_3_out), .in7(bit_extender_4_out),
    .in8(shifter_1_out), .in9(xor_1_out), .in10(shifter_2_out), .in11(shifter_3_out),
    .in12(bit_extender_5_out), .in13(bit_extender_6_out), .out(ALUOutput), .sel(ALUOperation));  // open: in14, in15
endmodule

module Register_File (
  input  WriteReg_CU,
  input  [4:0] WriteAddress,
  input  [31:0] WriteData,
  input  CLK,
  input  [4:0] ReadReg1,
  input  Reset,
  input  [4:0] ReadReg2,
  output [31:0] ReadData1,
  output [31:0] ReadData2,
  output [31:0] out_10
);

  wire and_1_out, and_2_out, and_3_out, and_4_out, and_5_out, and_6_out, and_7_out, and_8_out, and_9_out,
       and_10_out, and_11_out, and_12_out, and_13_out, and_14_out, and_15_out, and_16_out, and_17_out,
       and_18_out, and_19_out, and_20_out, and_21_out, and_22_out, and_23_out, and_24_out, and_25_out,
       and_26_out, and_27_out, and_28_out, and_29_out, and_30_out, and_31_out, and_32_out, decoder_1_out0,
       decoder_1_out1, decoder_1_out2, decoder_1_out3, decoder_1_out4, decoder_1_out5, decoder_1_out6,
       decoder_1_out7, decoder_1_out8, decoder_1_out9, decoder_1_out10, decoder_1_out11, decoder_1_out12,
       decoder_1_out13, decoder_1_out14, decoder_1_out15, decoder_1_out16, decoder_1_out17, decoder_1_out18,
       decoder_1_out19, decoder_1_out20, decoder_1_out21, decoder_1_out22, decoder_1_out23, decoder_1_out24,
       decoder_1_out25, decoder_1_out26, decoder_1_out27, decoder_1_out28, decoder_1_out29, decoder_1_out30,
       decoder_1_out31;
  wire [31:0] register_1_q, register_2_q, register_3_q, register_5_q, register_6_q, register_7_q,
       register_8_q, register_9_q, register_10_q, register_11_q, register_12_q, register_13_q, register_14_q,
       register_15_q, register_16_q, register_17_q, register_18_q, register_19_q, register_20_q,
       register_21_q, register_22_q, register_23_q, register_24_q, register_25_q, register_26_q,
       register_27_q, register_28_q, register_29_q, register_30_q, register_31_q, register_32_q;

  Decoder #(.select(5)) decoder_1 (
    .out0(decoder_1_out0), .out1(decoder_1_out1), .out2(decoder_1_out2), .out3(decoder_1_out3),
    .out4(decoder_1_out4), .out5(decoder_1_out5), .out6(decoder_1_out6), .out7(decoder_1_out7),
    .out8(decoder_1_out8), .out9(decoder_1_out9), .out10(decoder_1_out10), .out11(decoder_1_out11),
    .out12(decoder_1_out12), .out13(decoder_1_out13), .out14(decoder_1_out14), .out15(decoder_1_out15),
    .out16(decoder_1_out16), .out17(decoder_1_out17), .out18(decoder_1_out18), .out19(decoder_1_out19),
    .out20(decoder_1_out20), .out21(decoder_1_out21), .out22(decoder_1_out22), .out23(decoder_1_out23),
    .out24(decoder_1_out24), .out25(decoder_1_out25), .out26(decoder_1_out26), .out27(decoder_1_out27),
    .out28(decoder_1_out28), .out29(decoder_1_out29), .out30(decoder_1_out30), .out31(decoder_1_out31),
    .sel(WriteAddress));  // open: en
  and and_1 (and_1_out, decoder_1_out0, WriteReg_CU);
  and and_2 (and_2_out, decoder_1_out1, WriteReg_CU);
  and and_3 (and_3_out, decoder_1_out2, WriteReg_CU);
  and and_4 (and_4_out, decoder_1_out3, WriteReg_CU);
  and and_5 (and_5_out, decoder_1_out4, WriteReg_CU);
  and and_6 (and_6_out, decoder_1_out5, WriteReg_CU);
  and and_7 (and_7_out, decoder_1_out6, WriteReg_CU);
  and and_8 (and_8_out, decoder_1_out7, WriteReg_CU);
  and and_9 (and_9_out, decoder_1_out8, WriteReg_CU);
  and and_10 (and_10_out, decoder_1_out9, WriteReg_CU);
  and and_11 (and_11_out, decoder_1_out10, WriteReg_CU);
  and and_12 (and_12_out, decoder_1_out11, WriteReg_CU);
  and and_13 (and_13_out, decoder_1_out12, WriteReg_CU);
  and and_14 (and_14_out, decoder_1_out13, WriteReg_CU);
  and and_15 (and_15_out, decoder_1_out14, WriteReg_CU);
  and and_16 (and_16_out, decoder_1_out15, WriteReg_CU);
  and and_17 (and_17_out, decoder_1_out16, WriteReg_CU);
  and and_18 (and_18_out, decoder_1_out17, WriteReg_CU);
  and and_19 (and_19_out, decoder_1_out18, WriteReg_CU);
  and and_20 (and_20_out, decoder_1_out19, WriteReg_CU);
  and and_21 (and_21_out, decoder_1_out20, WriteReg_CU);
  and and_22 (and_22_out, decoder_1_out21, WriteReg_CU);
  and and_23 (and_23_out, decoder_1_out22, WriteReg_CU);
  and and_24 (and_24_out, decoder_1_out23, WriteReg_CU);
  and and_25 (and_25_out, decoder_1_out24, WriteReg_CU);
  and and_26 (and_26_out, decoder_1_out25, WriteReg_CU);
  and and_27 (and_27_out, decoder_1_out26, WriteReg_CU);
  and and_28 (and_28_out, decoder_1_out27, WriteReg_CU);
  and and_29 (and_29_out, decoder_1_out28, WriteReg_CU);
  and and_30 (and_30_out, decoder_1_out29, WriteReg_CU);
  and and_31 (and_31_out, decoder_1_out30, WriteReg_CU);
  and and_32 (and_32_out, decoder_1_out31, WriteReg_CU);
  Register #(.width(32)) register_1 (.D(WriteData), .en(and_1_out), .Q(register_1_q), .clk(CLK), .clr(Reset));
  Register #(.width(32)) register_2 (.D(WriteData), .en(and_2_out), .Q(register_2_q), .clk(CLK), .clr(Reset));
  Register #(.width(32)) register_3 (.D(WriteData), .en(and_3_out), .Q(register_3_q), .clk(CLK), .clr(Reset));
  Register #(.width(32)) register_4 (.D(WriteData), .en(and_4_out), .Q(out_10), .clk(CLK), .clr(Reset));
  Register #(.width(32)) register_5 (.D(WriteData), .en(and_5_out), .Q(register_5_q), .clk(CLK), .clr(Reset));
  Register #(.width(32)) register_6 (.D(WriteData), .en(and_6_out), .Q(register_6_q), .clk(CLK), .clr(Reset));
  Register #(.width(32)) register_7 (.D(WriteData), .en(and_7_out), .Q(register_7_q), .clk(CLK), .clr(Reset));
  Register #(.width(32)) register_8 (.D(WriteData), .en(and_8_out), .Q(register_8_q), .clk(CLK), .clr(Reset));
  Register #(.width(32)) register_9 (.D(WriteData), .en(and_9_out), .Q(register_9_q), .clk(CLK), .clr(Reset));
  Register #(.width(32)) register_10 (.D(WriteData), .en(and_10_out), .Q(register_10_q), .clk(CLK), .clr(Reset));
  Register #(.width(32)) register_11 (.D(WriteData), .en(and_11_out), .Q(register_11_q), .clk(CLK), .clr(Reset));
  Register #(.width(32)) register_12 (.D(WriteData), .en(and_12_out), .Q(register_12_q), .clk(CLK), .clr(Reset));
  Register #(.width(32)) register_13 (.D(WriteData), .en(and_13_out), .Q(register_13_q), .clk(CLK), .clr(Reset));
  Register #(.width(32)) register_14 (.D(WriteData), .en(and_14_out), .Q(register_14_q), .clk(CLK), .clr(Reset));
  Register #(.width(32)) register_15 (.D(WriteData), .en(and_15_out), .Q(register_15_q), .clk(CLK), .clr(Reset));
  Register #(.width(32)) register_16 (.D(WriteData), .en(and_16_out), .Q(register_16_q), .clk(CLK), .clr(Reset));
  Register #(.width(32)) register_17 (.D(WriteData), .en(and_17_out), .Q(register_17_q), .clk(CLK), .clr(Reset));
  Register #(.width(32)) register_18 (.D(WriteData), .en(and_18_out), .Q(register_18_q), .clk(CLK), .clr(Reset));
  Register #(.width(32)) register_19 (.D(WriteData), .en(and_19_out), .Q(register_19_q), .clk(CLK), .clr(Reset));
  Register #(.width(32)) register_20 (.D(WriteData), .en(and_20_out), .Q(register_20_q), .clk(CLK), .clr(Reset));
  Register #(.width(32)) register_21 (.D(WriteData), .en(and_21_out), .Q(register_21_q), .clk(CLK), .clr(Reset));
  Register #(.width(32)) register_22 (.D(WriteData), .en(and_22_out), .Q(register_22_q), .clk(CLK), .clr(Reset));
  Register #(.width(32)) register_23 (.D(WriteData), .en(and_23_out), .Q(register_23_q), .clk(CLK), .clr(Reset));
  Register #(.width(32)) register_24 (.D(WriteData), .en(and_24_out), .Q(register_24_q), .clk(CLK), .clr(Reset));
  Register #(.width(32)) register_25 (.D(WriteData), .en(and_25_out), .Q(register_25_q), .clk(CLK), .clr(Reset));
  Register #(.width(32)) register_26 (.D(WriteData), .en(and_26_out), .Q(register_26_q), .clk(CLK), .clr(Reset));
  Register #(.width(32)) register_27 (.D(WriteData), .en(and_27_out), .Q(register_27_q), .clk(CLK), .clr(Reset));
  Register #(.width(32)) register_28 (.D(WriteData), .en(and_28_out), .Q(register_28_q), .clk(CLK), .clr(Reset));
  Register #(.width(32)) register_29 (.D(WriteData), .en(and_29_out), .Q(register_29_q), .clk(CLK), .clr(Reset));
  Register #(.width(32)) register_30 (.D(WriteData), .en(and_30_out), .Q(register_30_q), .clk(CLK), .clr(Reset));
  Register #(.width(32)) register_31 (.D(WriteData), .en(and_31_out), .Q(register_31_q), .clk(CLK), .clr(Reset));
  Register #(.width(32)) register_32 (.D(WriteData), .en(and_32_out), .Q(register_32_q), .clk(CLK), .clr(Reset));
  Multiplexer #(.select(5), .width(32)) multiplexer_1 (
    .in0(register_1_q), .in1(register_2_q), .in2(register_3_q), .in3(out_10), .in4(register_5_q),
    .in5(register_6_q), .in6(register_7_q), .in7(register_8_q), .in8(register_9_q), .in9(register_10_q),
    .in10(register_11_q), .in11(register_12_q), .in12(register_13_q), .in13(register_14_q),
    .in14(register_15_q), .in15(register_16_q), .in16(register_17_q), .in17(register_18_q),
    .in18(register_19_q), .in19(register_20_q), .in20(register_21_q), .in21(register_22_q),
    .in22(register_23_q), .in23(register_24_q), .in24(register_25_q), .in25(register_26_q),
    .in26(register_27_q), .in27(register_28_q), .in28(register_29_q), .in29(register_30_q),
    .in30(register_31_q), .in31(register_32_q), .out(ReadData1), .sel(ReadReg1));  // open: en
  Multiplexer #(.select(5), .width(32)) multiplexer_2 (
    .in0(register_1_q), .in1(register_2_q), .in2(register_3_q), .in3(out_10), .in4(register_5_q),
    .in5(register_6_q), .in6(register_7_q), .in7(register_8_q), .in8(register_9_q), .in9(register_10_q),
    .in10(register_11_q), .in11(register_12_q), .in12(register_13_q), .in13(register_14_q),
    .in14(register_15_q), .in15(register_16_q), .in16(register_17_q), .in17(register_18_q),
    .in18(register_19_q), .in19(register_20_q), .in20(register_21_q), .in21(register_22_q),
    .in22(register_23_q), .in23(register_24_q), .in24(register_25_q), .in25(register_26_q),
    .in26(register_27_q), .in27(register_28_q), .in28(register_29_q), .in29(register_30_q),
    .in30(register_31_q), .in31(register_32_q), .out(ReadData2), .sel(ReadReg2));  // open: en
endmodule

module Immediate_Generator (
  input  [31:0] Instruction,
  output [31:0] ImmediateOut
);

  wire not_1_out;
  wire [1:0] S0_out;
  wire [31:0] I_TYPE, S_TYPE, SB_TYPE, UJ_TYPE;

  not not_1 (not_1_out, Instruction[2]);
  and S0 (S0_out[0], Instruction[5], not_1_out);
  xor S1 (S0_out[1], Instruction[6], Instruction[2]);
  assign I_TYPE = {{20{Instruction[31]}}, Instruction[31:20]};  // Bit_Extender bit_extender_1
  assign S_TYPE = {{20{Instruction[31]}}, {Instruction[31:25], Instruction[11:7]}};  // Bit_Extender bit_extender_2
  assign SB_TYPE = {{19{Instruction[31]}}, {Instruction[31], Instruction[7], Instruction[30:25], Instruction[11:8], 1'b0}};  // Bit_Extender bit_extender_3
  assign UJ_TYPE = {{11{Instruction[31]}}, {Instruction[31], Instruction[19:12], Instruction[20], Instruction[30:21], 1'b0}};  // Bit_Extender bit_extender_4
  Multiplexer #(.select(3), .width(32), .enable("false")) multiplexer_1 (
    .in0(I_TYPE), .in1(S_TYPE), .in2({Instruction[31:12], {12{1'b0}}}), .in3(SB_TYPE), .in4(UJ_TYPE),
    .out(ImmediateOut), .sel({Instruction[3], S0_out}));  // open: in5, in6, in7

  // Other names for the same wires on the sheet: U_TYPE[31:12] = Instruction[31:12]
endmodule

module Control_Unit (
  input  [6:0] OpcodeInput,
  output RS1,
  output Branch,
  output RetAddr,
  output MemToReg,
  output UpperImm,
  output JumpReg,
  output MemWrite,
  output RS2,
  output RegWrite,
  output A2,
  output A1,
  output A0,
  output Jump
);

  wire and_1_out, and_2_out, and_3_out, and_9_out, nand_1_out, not_1_out, not_2_out, not_3_out, not_4_out,
       not_5_out, not_6_out, not_7_out, not_8_out, not_9_out, or_2_out, xor_1_out;

  not not_1 (not_1_out, OpcodeInput[2]);
  not not_2 (not_2_out, OpcodeInput[4]);
  not not_3 (not_3_out, OpcodeInput[5]);
  and and_1 (and_1_out, not_1_out, OpcodeInput[4], OpcodeInput[5]);
  and and_2 (and_2_out, not_2_out, not_3_out);
  or or_1 (A2, OpcodeInput[3], and_3_out, and_2_out, and_1_out);
  not not_4 (not_4_out, OpcodeInput[3]);
  not not_5 (not_5_out, OpcodeInput[4]);
  and and_3 (and_3_out, OpcodeInput[2], not_4_out, not_5_out);
  not not_6 (not_6_out, OpcodeInput[4]);
  and and_4 (RetAddr, OpcodeInput[2], OpcodeInput[6]);
  nor nor_1 (MemToReg, OpcodeInput[4], OpcodeInput[5]);
  not not_7 (not_7_out, OpcodeInput[3]);
  not not_8 (not_8_out, OpcodeInput[4]);
  not not_9 (not_9_out, OpcodeInput[6]);
  or or_2 (or_2_out, OpcodeInput[4], OpcodeInput[6]);
  nand nand_1 (nand_1_out, OpcodeInput[5], not_6_out);
  xor xor_1 (xor_1_out, OpcodeInput[2], OpcodeInput[6]);
  not not_10 (RS1, OpcodeInput[2]);
  and and_5 (UpperImm, OpcodeInput[2], OpcodeInput[4], OpcodeInput[5]);
  and and_6 (JumpReg, OpcodeInput[2], not_7_out, not_8_out);
  and and_7 (MemWrite, not_8_out, OpcodeInput[5], not_9_out);
  or or_3 (RegWrite, OpcodeInput[2], nand_1_out);
  or or_4 (A1, and_3_out, xor_1_out, and_2_out);
  and and_8 (RS2, RS1, OpcodeInput[5], or_2_out);
  and and_9 (and_9_out, RS1, OpcodeInput[5]);
  or or_5 (A0, and_3_out, and_9_out);

  assign Branch = OpcodeInput[6];
  assign Jump = OpcodeInput[3];
endmodule

module ALU_Control (
  input  [2:0] ALUOp,
  input  [2:0] Function3,
  input  [6:0] Function7,
  output [3:0] ALUOperation
);

  wire _000_out, _001_out, _010_out, _011_out, _100_out, _101_out, _110_out, _111_out, and_1_out, and_2_out,
       and_3_out, and_4_out, and_5_out, and_6_out, and_7_out, and_8_out, and_9_out, and_10_out, and_11_out,
       and_12_out, and_13_out, and_14_out, I_type_out, JalR_type_out, Load_type_out, not_1_out, not_2_out,
       not_3_out, not_4_out, not_5_out, not_6_out, not_7_out, or_1_out, or_2_out, or_3_out, or_4_out,
       or_5_out, or_6_out, R_type_out, S_type_out, SB_type_out, U_type_out, UJ_type_out;

  not not_1 (not_1_out, Function7[5]);
  not not_2 (not_2_out, Function3[2]);
  not not_3 (not_3_out, Function3[0]);
  not not_4 (not_4_out, Function3[1]);
  not not_5 (not_5_out, ALUOp[1]);
  not not_6 (not_6_out, ALUOp[2]);
  not not_7 (not_7_out, ALUOp[0]);
  and I_type (I_type_out, not_7_out, not_5_out, not_6_out);
  and R_type (R_type_out, ALUOp[2], not_5_out, ALUOp[0]);
  and _110 (_110_out, Function3[2], Function3[1], not_3_out);
  and _111 (_111_out, Function3[2], Function3[1], Function3[0]);
  and _100 (_100_out, Function3[2], not_4_out, not_3_out);
  and _000 (_000_out, not_2_out, not_4_out, not_3_out);
  and SB_type (SB_type_out, not_6_out, ALUOp[1], ALUOp[0]);
  and _101 (_101_out, Function3[2], not_4_out, Function3[0]);
  and _001 (_001_out, not_2_out, not_4_out, Function3[0]);
  and _011 (_011_out, not_2_out, Function3[1], Function3[0]);
  and _010 (_010_out, not_2_out, Function3[1], not_3_out);
  and U_type (U_type_out, not_7_out, ALUOp[1], not_6_out);
  and UJ_type (UJ_type_out, not_7_out, not_5_out, ALUOp[2]);
  and S_type (S_type_out, not_6_out, not_5_out, ALUOp[0]);
  and Load_type (Load_type_out, ALUOp[2], ALUOp[1], not_7_out);
  and JalR_type (JalR_type_out, ALUOp[2], ALUOp[1], ALUOp[0]);
  or or_1 (or_1_out, I_type_out, R_type_out);
  or or_2 (or_2_out, or_1_out, SB_type_out);
  or or_3 (or_3_out, _100_out, _010_out);
  or or_4 (or_4_out, Load_type_out, or_1_out, U_type_out, S_type_out, UJ_type_out, JalR_type_out);
  or or_5 (or_5_out, _000_out, _010_out);
  and and_1 (and_1_out, or_1_out, _110_out);
  and and_2 (and_2_out, or_1_out, _111_out);
  and and_3 (and_3_out, or_1_out, _100_out);
  and and_4 (and_4_out, R_type_out, _000_out, Function7[5]);
  and and_5 (and_5_out, SB_type_out, _101_out);
  and and_6 (and_6_out, SB_type_out, _000_out);
  and and_7 (and_7_out, SB_type_out, _001_out);
  and and_8 (and_8_out, SB_type_out, _101_out);
  and and_9 (and_9_out, or_1_out, _011_out);
  and and_10 (and_10_out, or_1_out, not_1_out, _101_out);
  and and_11 (and_11_out, or_1_out, _101_out, Function7[5]);
  and and_12 (and_12_out, or_1_out, _001_out);
  and and_13 (and_13_out, or_2_out, or_3_out);
  and and_14 (and_14_out, or_4_out, or_5_out);
  or or_6 (or_6_out, and_14_out, U_type_out);
  Priority_Encoder #(.select(4)) priority_encoder_1 (
    .in0(and_1_out), .in1(and_2_out), .in2(or_6_out), .in3(and_4_out), .in4(and_5_out), .in5(and_13_out),
    .in6(and_6_out), .in7(and_7_out), .in8(and_12_out), .in9(and_3_out), .in10(and_10_out),
    .in11(and_11_out), .in12(and_8_out), .in13(and_9_out), .out(ALUOperation));  // open: in14, in15, gs, en_out, en_in

  // Notes on the sheet:
  //   OR
  //   AND
  //   XOR
  //   SUB
  //   GE
  //   EQ
  //   NE
  //   GEU
  //   LTU
  //   SRL
  //   SRA
  //   SLL
  //   LT
  //   ADD
endmodule
